// Logisim project Calculator.circ as structural Verilog: 6 circuits, main circuit CALCULATOR
module main (
  input  B0,
  input  B1,
  input  B2,
  input  B3,
  input  B4,
  input  B5,
  input  B6,
  input  B7
);

  wire b8tctobcd_1_p0, b8tctobcd_1_p1, b8tctobcd_1_p2, b8tctobcd_1_p3, b8tctobcd_1_p4, b8tctobcd_1_p5,
       b8tctobcd_1_p6, b8tctobcd_1_p7, b8tctobcd_1_p8, b8tctobcd_1_p9, n7447_1_pin2, n7447_1_pin3,
       n7447_1_pin9, n7447_1_pin10, n7447_1_pin11, n7447_1_pin12, n7447_1_pin13, n7447_1_pin14,
       n7447_1_pin15, n7447_2_pin9, n7447_2_pin10, n7447_2_pin11, n7447_2_pin12, n7447_2_pin13,
       n7447_2_pin14, n7447_2_pin15, n7447_3_pin9, n7447_3_pin10, n7447_3_pin11, n7447_3_pin12,
       n7447_3_pin13, n7447_3_pin14, n7447_3_pin15, not_1_out, not_2_out, not_3_out, not_4_out, not_5_out,
       not_6_out, not_7_out, not_8_out, not_9_out, not_10_out, not_11_out, not_12_out, not_13_out,
       not_14_out, not_15_out, not_16_out, not_17_out, not_18_out, not_19_out, not_20_out, not_21_out;

  B8TCTOBCD b8tctobcd_1 (
    .B0(B0), .B1(B1), .B2(B2), .B3(B3), .B4(B4), .B5(B5), .B6(B6), .B7(B7), .P0(b8tctobcd_1_p0),
    .P1(b8tctobcd_1_p1), .P2(b8tctobcd_1_p2), .P3(b8tctobcd_1_p3), .P4(b8tctobcd_1_p4), .P5(b8tctobcd_1_p5),
    .P6(b8tctobcd_1_p6), .P7(b8tctobcd_1_p7), .P8(b8tctobcd_1_p8), .P9(b8tctobcd_1_p9));
  _7_Segment_Display u_7_segment_display_1 (.g(B7));  // open: f, a, b, e, d, c, dp
  not not_1 (not_1_out, n7447_1_pin9);
  not not_2 (not_2_out, n7447_1_pin10);
  not not_3 (not_3_out, n7447_1_pin11);
  not not_4 (not_4_out, n7447_1_pin12);
  _7_Segment_Display u_7_segment_display_2 (
    .g(not_6_out), .f(not_7_out), .a(not_5_out), .b(not_4_out), .e(not_1_out), .d(not_2_out), .c(not_3_out));  // open: dp
  _7447 u_7447_1 (
    .pin1(b8tctobcd_1_p9), .pin2(n7447_1_pin2), .pin3(n7447_1_pin3), .pin4(n7447_1_pin3),
    .pin5(n7447_1_pin3), .pin6(n7447_1_pin2), .pin7(b8tctobcd_1_p8), .pin15(n7447_1_pin15),
    .pin14(n7447_1_pin14), .pin13(n7447_1_pin13), .pin12(n7447_1_pin12), .pin11(n7447_1_pin11),
    .pin10(n7447_1_pin10), .pin9(n7447_1_pin9));
  not not_5 (not_5_out, n7447_1_pin13);
  not not_6 (not_6_out, n7447_1_pin14);
  not not_7 (not_7_out, n7447_1_pin15);
  not not_8 (not_8_out, n7447_2_pin9);
  not not_9 (not_9_out, n7447_2_pin10);
  not not_10 (not_10_out, n7447_2_pin11);
  not not_11 (not_11_out, n7447_2_pin12);
  not not_12 (not_12_out, n7447_2_pin13);
  not not_13 (not_13_out, n7447_2_pin14);
  _7_Segment_Display u_7_segment_display_3 (
    .g(not_13_out), .f(not_14_out), .a(not_12_out), .b(not_11_out), .e(not_8_out), .d(not_9_out),
    .c(not_10_out));  // open: dp
  _7447 u_7447_2 (
    .pin1(b8tctobcd_1_p5), .pin2(b8tctobcd_1_p6), .pin3(n7447_1_pin3), .pin4(n7447_1_pin3),
    .pin5(n7447_1_pin3), .pin6(b8tctobcd_1_p7), .pin7(b8tctobcd_1_p4), .pin15(n7447_2_pin15),
    .pin14(n7447_2_pin14), .pin13(n7447_2_pin13), .pin12(n7447_2_pin12), .pin11(n7447_2_pin11),
    .pin10(n7447_2_pin10), .pin9(n7447_2_pin9));
  not not_14 (not_14_out, n7447_2_pin15);
  not not_15 (not_15_out, n7447_3_pin9);
  not not_16 (not_16_out, n7447_3_pin10);
  not not_17 (not_17_out, n7447_3_pin11);
  not not_18 (not_18_out, n7447_3_pin12);
  _7_Segment_Display u_7_segment_display_4 (
    .g(not_21_out), .f(not_19_out), .a(not_20_out), .b(not_18_out), .e(not_15_out), .d(not_16_out),
    .c(not_17_out));  // open: dp
  _7447 u_7447_3 (
    .pin1(b8tctobcd_1_p1), .pin2(b8tctobcd_1_p2), .pin3(n7447_1_pin3), .pin4(n7447_1_pin3),
    .pin5(n7447_1_pin3), .pin6(b8tctobcd_1_p3), .pin7(b8tctobcd_1_p0), .pin15(n7447_3_pin15),
    .pin14(n7447_3_pin14), .pin13(n7447_3_pin13), .pin12(n7447_3_pin12), .pin11(n7447_3_pin11),
    .pin10(n7447_3_pin10), .pin9(n7447_3_pin9));
  not not_19 (not_19_out, n7447_3_pin15);
  not not_20 (not_20_out, n7447_3_pin13);
  not not_21 (not_21_out, n7447_3_pin14);
  // also tied to GND on the sheet: n7447_1_pin2
  // also tied to VCC on the sheet: n7447_1_pin3
endmodule

module ADD3 (
  input  A0,
  input  A1,
  input  A2,
  input  A3,
  output S0,
  output S1,
  output S2,
  output S3
);

  wire and_1_out, and_2_out, and_3_out, and_4_out, and_5_out, and_6_out, and_7_out, and_8_out, and_9_out,
       and_10_out, not_1_out, not_2_out, not_3_out, not_4_out;

  not not_1 (not_1_out, A0);
  not not_2 (not_2_out, A1);
  not not_3 (not_3_out, A2);
  not not_4 (not_4_out, A3);
  and and_1 (and_1_out, A2, A0);
  and and_2 (and_2_out, A2, A1);
  and and_3 (and_3_out, A2, not_2_out, not_1_out);
  and and_4 (and_4_out, A3, A0);
  and and_5 (and_5_out, not_3_out, A1);
  and and_6 (and_6_out, A1, A0);
  and and_7 (and_7_out, A3, not_1_out);
  and and_8 (and_8_out, not_4_out, not_3_out, A0);
  and and_9 (and_9_out, A3, not_1_out);
  and and_10 (and_10_out, A2, A1, not_1_out);
  or or_1 (S0, and_8_out, and_9_out, and_10_out);
  or or_2 (S1, and_5_out, and_6_out, and_7_out);
  or or_3 (S2, and_3_out, and_4_out);
  or or_4 (S3, and_1_out, A3, and_2_out);

  // Notes on the sheet:
  //   ADD
  //   If the amount is greater than or equal to 5
  //   3
endmodule

module B8TOBCD (
  input  B0,
  input  B1,
  input  B2,
  input  B3,
  input  B4,
  input  B5,
  input  B6,
  input  B7,
  output P0,
  output P1,
  output P2,
  output P3,
  output P4,
  output P5,
  output P6,
  output P7,
  output P8,
  output P9
);

  wire add3_1_s0, add3_1_s1, add3_1_s2, add3_1_s3, add3_2_s0, add3_2_s1, add3_2_s2, add3_2_s3, add3_3_s0,
       add3_3_s1, add3_3_s2, add3_3_s3, add3_4_s0, add3_4_s1, add3_4_s2, add3_4_s3, add3_5_s0, add3_5_s1,
       add3_5_s2;

  ADD3 add3_1 (.A1(B6), .A2(B7), .A3(1'b0), .A0(B5), .S0(add3_1_s0), .S1(add3_1_s1), .S2(add3_1_s2), .S3(add3_1_s3));
  ADD3 add3_2 (
    .A1(add3_1_s0), .A2(add3_1_s1), .A3(add3_1_s2), .A0(B4), .S0(add3_2_s0), .S1(add3_2_s1), .S2(add3_2_s2),
    .S3(add3_2_s3));
  ADD3 add3_3 (
    .A1(add3_2_s0), .A2(add3_2_s1), .A3(add3_2_s2), .A0(B3), .S0(add3_3_s0), .S1(add3_3_s1), .S2(add3_3_s2),
    .S3(add3_3_s3));
  ADD3 add3_4 (
    .A1(add3_3_s0), .A2(add3_3_s1), .A3(add3_3_s2), .A0(B2), .S0(add3_4_s0), .S1(add3_4_s1), .S2(add3_4_s2),
    .S3(add3_4_s3));
  ADD3 add3_5 (
    .A1(add3_2_s3), .A2(add3_1_s3), .A3(1'b0), .A0(add3_3_s3), .S0(add3_5_s0), .S1(add3_5_s1),
    .S2(add3_5_s2), .S3(P9));
  ADD3 add3_6 (.A1(add3_4_s0), .A2(add3_4_s1), .A3(add3_4_s2), .A0(B1), .S0(P1), .S1(P2), .S2(P3), .S3(P4));
  ADD3 add3_7 (.A1(add3_5_s0), .A2(add3_5_s1), .A3(add3_5_s2), .A0(add3_4_s3), .S0(P5), .S1(P6), .S2(P7), .S3(P8));

  assign P0 = B0;

  // Notes on the sheet:
  //   0
  //   0
  //   B8TOBCD
  //   Converts 8-bit unsigned binary to BCD
endmodule

module B8TCTOBCD (
  input  B0,
  input  B1,
  input  B2,
  input  B3,
  input  B4,
  input  B5,
  input  B6,
  input  B7,
  output P0,
  output P1,
  output P2,
  output P3,
  output P4,
  output P5,
  output P6,
  output P7,
  output P8,
  output P9
);

  wire [7:0] adder_1_out, multiplexer_1_out, not_1_out;

  assign not_1_out = ~{B7, B6, B5, B4, B3, B2, B1, B0};  // NOT_Gate not_1, 8 bits wide
  Adder adder_1 (.a(not_1_out), .b(8'h1), .out(adder_1_out));  // open: cin, cout
  Multiplexer #(.width(8)) multiplexer_1 (
    .in0({B7, B6, B5, B4, B3, B2, B1, B0}), .in1(adder_1_out), .out(multiplexer_1_out), .sel(B7));
  B8TOBCD b8tobcd_1 (
    .B0(multiplexer_1_out[0]), .B1(multiplexer_1_out[1]), .B2(multiplexer_1_out[2]),
    .B3(multiplexer_1_out[3]), .B4(multiplexer_1_out[4]), .B5(multiplexer_1_out[5]),
    .B6(multiplexer_1_out[6]), .B7(multiplexer_1_out[7]), .P0(P0), .P1(P1), .P2(P2), .P3(P3), .P4(P4),
    .P5(P5), .P6(P6), .P7(P7), .P8(P8), .P9(P9));

  // Notes on the sheet:
  //   B8TCTOBCD
  //   Converts 8-bit 2's com to BCD
endmodule

module CALCULATOR (
);

  wire add, and_1_out, and_2_out, and_3_out, and_4_out, b8tctobcd_1_p0, b8tctobcd_1_p1, b8tctobcd_1_p2,
       b8tctobcd_1_p3, b8tctobcd_1_p4, b8tctobcd_1_p5, b8tctobcd_1_p6, b8tctobcd_1_p7, b8tctobcd_1_p8,
       b8tctobcd_1_p9, back, c, ce, clock_1_out, controlled_buffer_1_out, controlled_buffer_23_out,
       controlled_buffer_26_out, controlled_buffer_31_out, controlled_buffer_33_out,
       controlled_buffer_35_out, d_ff_1_q, d_ff_1_qn, d_ff_2_q, ic7448_1_out_8, ic7448_1_out_9,
       ic7448_1_out_10, ic7448_1_out_11, ic7448_1_out_12, ic7448_1_out_13, ic7448_1_out_14, ic7448_2_out_8,
       ic7448_2_out_9, ic7448_2_out_10, ic7448_2_out_11, ic7448_2_out_12, ic7448_2_out_13, ic7448_2_out_14,
       ic7448_3_out_8, ic7448_3_out_9, ic7448_3_out_10, ic7448_3_out_11, ic7448_3_out_12, ic7448_3_out_13,
       ic7448_3_out_14, not_1_out, not_2_out, or_1_out, or_2_out, pull_resistor_2_node, pull_resistor_3_node,
       result, s_r_ff_1_q, s_r_ff_2_q, sub, x0, x1, x2, x3, x4, x5, x6, x7, x8, x9;
  wire [7:0] adder_1_out, adder_2_out, controlled_buffer_11_out, dbus, divider_1_out, multiplexer_1_out,
       multiplexer_2_out, multiplier_1_out, r1, r2, subtractor_1_out;

  assign controlled_buffer_1_out = x0 ? x0 : 1'bz;  // Controlled_Buffer controlled_buffer_1
  assign controlled_buffer_1_out = x1 ? x1 : 1'bz;  // Controlled_Buffer controlled_buffer_2
  assign controlled_buffer_1_out = x2 ? x2 : 1'bz;  // Controlled_Buffer controlled_buffer_3
  assign controlled_buffer_1_out = x3 ? x3 : 1'bz;  // Controlled_Buffer controlled_buffer_4
  assign controlled_buffer_1_out = x4 ? x4 : 1'bz;  // Controlled_Buffer controlled_buffer_5
  assign controlled_buffer_1_out = x5 ? x5 : 1'bz;  // Controlled_Buffer controlled_buffer_6
  assign controlled_buffer_1_out = x6 ? x6 : 1'bz;  // Controlled_Buffer controlled_buffer_7
  assign controlled_buffer_1_out = x7 ? x7 : 1'bz;  // Controlled_Buffer controlled_buffer_8
  assign controlled_buffer_1_out = x8 ? x8 : 1'bz;  // Controlled_Buffer controlled_buffer_9
  assign controlled_buffer_1_out = x9 ? x9 : 1'bz;  // Controlled_Buffer controlled_buffer_10
  Pull_Resistor pull_resistor_1 (.node(controlled_buffer_1_out));
  assign controlled_buffer_11_out = x0 ? {8{1'b0}} : 8'bz;  // Controlled_Buffer controlled_buffer_11
  assign controlled_buffer_11_out = x1 ? 8'h1 : 8'bz;  // Controlled_Buffer controlled_buffer_12
  assign controlled_buffer_11_out = x2 ? 8'h2 : 8'bz;  // Controlled_Buffer controlled_buffer_13
  assign controlled_buffer_11_out = x3 ? 8'h3 : 8'bz;  // Controlled_Buffer controlled_buffer_14
  assign controlled_buffer_11_out = x4 ? 8'h4 : 8'bz;  // Controlled_Buffer controlled_buffer_15
  assign controlled_buffer_11_out = x5 ? 8'h5 : 8'bz;  // Controlled_Buffer controlled_buffer_16
  assign controlled_buffer_11_out = x6 ? 8'h6 : 8'bz;  // Controlled_Buffer controlled_buffer_17
  assign controlled_buffer_11_out = x7 ? 8'h7 : 8'bz;  // Controlled_Buffer controlled_buffer_18
  assign controlled_buffer_11_out = x8 ? 8'h8 : 8'bz;  // Controlled_Buffer controlled_buffer_19
  Pull_Resistor pull_resistor_2 (.node(pull_resistor_2_node));
  assign controlled_buffer_11_out = x9 ? 8'h9 : 8'bz;  // Controlled_Buffer controlled_buffer_20
  assign pull_resistor_2_node = controlled_buffer_1_out ? controlled_buffer_1_out : 1'bz;  // Controlled_Buffer controlled_buffer_21
  assign pull_resistor_2_node = or_1_out ? or_1_out : 1'bz;  // Controlled_Buffer controlled_buffer_22
  or or_1 (or_1_out, sub, add);
  Button button_1 (.out(x1));
  Button button_2 (.out(x4));
  Button button_3 (.out(x7));
  Button button_4 (.out(x0));
  or or_2 (or_2_out, controlled_buffer_1_out, result, back);
  Register register_1 (
    .D(multiplexer_1_out), .clk(controlled_buffer_23_out), .Q(r2), .clr(pull_resistor_3_node));  // open: en
  and and_1 (and_1_out, and_4_out, or_2_out);
  assign controlled_buffer_23_out = and_1_out ? and_1_out : 1'bz;  // Controlled_Buffer controlled_buffer_23
  Pull_Resistor pull_resistor_3 (.node(pull_resistor_3_node));
  assign pull_resistor_2_node = result ? result : 1'bz;  // Controlled_Buffer controlled_buffer_24
  Clock clock_1 (.out(clock_1_out));
  assign pull_resistor_2_node = back ? back : 1'bz;  // Controlled_Buffer controlled_buffer_25
  assign controlled_buffer_26_out = add ? add : 1'bz;  // Controlled_Buffer controlled_buffer_26
  Button button_5 (.out(x2));
  Button button_6 (.out(x5));
  Button button_7 (.out(x8));
  Button button_8 (.out(add));
  Pull_Resistor pull_resistor_4 (.node(controlled_buffer_23_out));
  assign pull_resistor_3_node = ce ? ce : 1'bz;  // Controlled_Buffer controlled_buffer_27
  D_Flip_Flop d_ff_1 (
    .D(pull_resistor_2_node), .clk(clock_1_out), .Q(d_ff_1_q), .Qn(d_ff_1_qn));  // open: preset, reset
  not not_1 (not_1_out, clock_1_out);
  S_R_Flip_Flop s_r_ff_1 (
    .S(sub), .R(controlled_buffer_26_out), .clk(clock_1_out), .Q(s_r_ff_1_q));  // open: reset, Qn, preset
  Button button_9 (.out(x3));
  Button button_10 (.out(x6));
  Button button_11 (.out(x9));
  Button button_12 (.out(sub));
  Multiplier #(.mode("twosComplement")) multiplier_1 (.a(r2), .b(8'ha), .out(multiplier_1_out));  // open: cin, cout
  Divider divider_1 (.a(r2), .b(8'ha), .out(divider_1_out));  // open: upper, rem
  assign pull_resistor_3_node = and_2_out ? and_2_out : 1'bz;  // Controlled_Buffer controlled_buffer_28
  assign pull_resistor_3_node = c ? controlled_buffer_31_out : 1'bz;  // Controlled_Buffer controlled_buffer_29
  D_Flip_Flop d_ff_2 (.D(d_ff_1_qn), .clk(not_1_out), .Q(d_ff_2_q));  // open: Qn, preset, reset
  assign controlled_buffer_26_out = controlled_buffer_33_out ? controlled_buffer_33_out : 1'bz;  // Controlled_Buffer controlled_buffer_30
  Pull_Resistor pull_resistor_5 (.node(controlled_buffer_26_out));
  Multiplexer #(.width(8)) multiplexer_1 (.in0(multiplexer_2_out), .in1(dbus), .out(multiplexer_1_out), .sel(result));
  Adder adder_1 (.a(controlled_buffer_11_out), .b(multiplier_1_out), .out(adder_1_out));  // open: cin, cout
  Register register_2 (.D(dbus), .clk(and_2_out), .Q(r1), .clr(controlled_buffer_31_out));  // open: en
  assign controlled_buffer_31_out = and_3_out ? and_3_out : 1'bz;  // Controlled_Buffer controlled_buffer_31
  and and_2 (and_2_out, and_4_out, or_1_out);
  and and_3 (and_3_out, controlled_buffer_33_out, and_4_out);
  S_R_Flip_Flop s_r_ff_2 (
    .S(or_1_out), .R(controlled_buffer_33_out), .clk(clock_1_out), .Q(s_r_ff_2_q));  // open: reset, Qn, preset
  Button button_13 (.out(c));
  Button button_14 (.out(ce));
  Button button_15 (.out(back));
  Button button_16 (.out(result));
  Multiplexer #(.width(8)) multiplexer_2 (.in0(adder_1_out), .in1(divider_1_out), .out(multiplexer_2_out), .sel(back));
  assign controlled_buffer_31_out = c ? c : 1'bz;  // Controlled_Buffer controlled_buffer_32
  and and_4 (and_4_out, d_ff_1_q, d_ff_2_q);
  assign controlled_buffer_33_out = controlled_buffer_31_out ? controlled_buffer_31_out : 1'bz;  // Controlled_Buffer controlled_buffer_33
  assign controlled_buffer_33_out = result ? result : 1'bz;  // Controlled_Buffer controlled_buffer_34
  Adder adder_2 (.a(r1), .b(r2), .out(adder_2_out));  // open: cin, cout
  Subtractor subtractor_1 (.a(r1), .b(r2), .out(subtractor_1_out));  // open: bin, bout
  Pull_Resistor pull_resistor_6 (.node(controlled_buffer_31_out));
  Pull_Resistor pull_resistor_7 (.node(controlled_buffer_33_out));
  assign controlled_buffer_35_out = s_r_ff_2_q ? s_r_ff_1_q : 1'bz;  // Controlled_Buffer controlled_buffer_35
  B8TCTOBCD b8tctobcd_1 (
    .B0(r2[0]), .B1(r2[1]), .B2(r2[2]), .B3(r2[3]), .B4(r2[4]), .B5(r2[5]), .B6(r2[6]), .B7(r2[7]),
    .P0(b8tctobcd_1_p0), .P1(b8tctobcd_1_p1), .P2(b8tctobcd_1_p2), .P3(b8tctobcd_1_p3), .P4(b8tctobcd_1_p4),
    .P5(b8tctobcd_1_p5), .P6(b8tctobcd_1_p6), .P7(b8tctobcd_1_p7), .P8(b8tctobcd_1_p8), .P9(b8tctobcd_1_p9));
  _7_Segment_Display u_7_segment_display_1 (.g(r2[7]));  // open: f, a, b, e, d, c, dp
  _7_Segment_Display u_7_segment_display_2 (
    .g(controlled_buffer_35_out), .f(not_2_out), .a(not_2_out), .b(not_2_out), .e(not_2_out), .d(not_2_out),
    .c(not_2_out), .dp(not_2_out));
  not not_2 (not_2_out, controlled_buffer_35_out);
  Multiplexer #(.width(8)) multiplexer_3 (.in0(adder_2_out), .in1(subtractor_1_out), .out(dbus), .sel(s_r_ff_1_q));
  IC7448 ic7448_1 (
    .in_1(b8tctobcd_1_p1), .in_2(b8tctobcd_1_p2), .in_3(1'b1), .in_4(1'b1), .in_5(1'b1),
    .in_6(b8tctobcd_1_p3), .in_7(b8tctobcd_1_p0), .out_8(ic7448_1_out_8), .out_9(ic7448_1_out_9),
    .out_10(ic7448_1_out_10), .out_11(ic7448_1_out_11), .out_12(ic7448_1_out_12), .out_13(ic7448_1_out_13),
    .out_14(ic7448_1_out_14));
  IC7448 ic7448_2 (
    .in_1(b8tctobcd_1_p5), .in_2(b8tctobcd_1_p6), .in_3(1'b1), .in_4(1'b1), .in_5(1'b1),
    .in_6(b8tctobcd_1_p7), .in_7(b8tctobcd_1_p4), .out_8(ic7448_2_out_8), .out_9(ic7448_2_out_9),
    .out_10(ic7448_2_out_10), .out_11(ic7448_2_out_11), .out_12(ic7448_2_out_12), .out_13(ic7448_2_out_13),
    .out_14(ic7448_2_out_14));
  IC7448 ic7448_3 (
    .in_1(b8tctobcd_1_p9), .in_2(1'b0), .in_3(1'b1), .in_4(1'b1), .in_5(1'b1), .in_6(1'b0),
    .in_7(b8tctobcd_1_p8), .out_8(ic7448_3_out_8), .out_9(ic7448_3_out_9), .out_10(ic7448_3_out_10),
    .out_11(ic7448_3_out_11), .out_12(ic7448_3_out_12), .out_13(ic7448_3_out_13), .out_14(ic7448_3_out_14));
  _7_Segment_Display u_7_segment_display_3 (
    .g(ic7448_3_out_9), .f(ic7448_3_out_8), .a(ic7448_3_out_10), .b(ic7448_3_out_11), .e(ic7448_3_out_14),
    .d(ic7448_3_out_13), .c(ic7448_3_out_12));  // open: dp
  _7_Segment_Display u_7_segment_display_4 (
    .g(ic7448_2_out_9), .f(ic7448_2_out_8), .a(ic7448_2_out_10), .b(ic7448_2_out_11), .e(ic7448_2_out_14),
    .d(ic7448_2_out_13), .c(ic7448_2_out_12));  // open: dp
  _7_Segment_Display u_7_segment_display_5 (
    .g(ic7448_1_out_9), .f(ic7448_1_out_8), .a(ic7448_1_out_10), .b(ic7448_1_out_11), .e(ic7448_1_out_14),
    .d(ic7448_1_out_13), .c(ic7448_1_out_12));  // open: dp
endmodule

module IC7448 (
  input  in_1,
  input  in_2,
  input  in_3,
  input  in_4,
  input  in_5,
  input  in_6,
  input  in_7,
  output out_8,
  output out_9,
  output out_10,
  output out_11,
  output out_12,
  output out_13,
  output out_14
);

  wire n7447_1_pin9, n7447_1_pin10, n7447_1_pin11, n7447_1_pin12, n7447_1_pin13, n7447_1_pin14, n7447_1_pin15;

  _7447 u_7447_1 (
    .pin1(in_1), .pin2(in_2), .pin3(in_3), .pin4(in_4), .pin5(in_5), .pin6(in_6), .pin7(in_7),
    .pin15(n7447_1_pin15), .pin14(n7447_1_pin14), .pin13(n7447_1_pin13), .pin12(n7447_1_pin12),
    .pin11(n7447_1_pin11), .pin10(n7447_1_pin10), .pin9(n7447_1_pin9));
  not not_1 (out_8, n7447_1_pin15);
  not not_2 (out_9, n7447_1_pin14);
  not not_3 (out_10, n7447_1_pin13);
  not not_4 (out_11, n7447_1_pin12);
  not not_5 (out_12, n7447_1_pin11);
  not not_6 (out_13, n7447_1_pin10);
  not not_7 (out_14, n7447_1_pin9);
endmodule
